# Fritzing sketch diseño1-arduinoUno (saved by Fritzing 0.9.3b)
breadboards: 1

parts:
  Componente1 = Arduino Uno (Rev3)
  kEYPAD_MATRICIAL_1 = KEYPAD 4x3
  Componente2 = Bluetooth HC-05 Macho
  Componente3 = RFID-RC522-v2
  R2 = Resistor [tolerance=±5% resistance=2.2k package="2512 [SMD]"]
  R1 = Resistor [tolerance=±5% resistance=1k package="2512 [SMD]"]

nets:
  N1: Componente1.D8, kEYPAD_MATRICIAL_1.col1
  N2: Componente1.D9_PWM, Componente3.RST
  N3: Componente1.D10_PWM/SS, Componente3.SDA
  N4: Componente1.D11_PWM/MOSI, Componente3.MOSI
  N5: Componente1.D12/MISO, Componente3.MISO
  N6: Componente1.D13/SCK, Componente3.SCK
  N7: Componente1.D0/RX, Componente2.TXD
  N8: Componente1.D1/TX, R1.Pin_0
  N9: Componente1.D2, kEYPAD_MATRICIAL_1.arrow4
  N10: Componente1.D3_PWM, kEYPAD_MATRICIAL_1.arrow3
  N11: Componente1.D4, kEYPAD_MATRICIAL_1.col3
  N12: Componente1.D5_PWM, kEYPAD_MATRICIAL_1.arrow2
  N13: Componente1.D6_PWM, kEYPAD_MATRICIAL_1.col2
  N14: Componente1.D7, kEYPAD_MATRICIAL_1.arrow1
  5V: Componente1.5V, Componente2.VCC, Componente3.3.3V
  GND: Componente1.GND, Componente2.GND, Componente3.GND, R2.Pin_1
  N15: Componente2.RXD, R2.Pin_0, R1.Pin_1

custom parts:
  KEYPAD 4x3: KEYPAD matricial de 12 botones, 4 filas x 3 columnas
  RFID-RC522-v2: A simple China made RFID-RC522 Reader; do check the pin labels, as this is a MFRC522 based clone.
