# Fritzing sketch diseño2-arduinoMega (saved by Fritzing 0.9.3b)
breadboards: 1

parts:
  kEYPAD_MATRICIAL_1 = KEYPAD 4x3
  Componente2 = Bluetooth HC-05 Macho
  Componente3 = RFID-RC522-v2
  R1 = Resistor [tolerance=±5% resistance=1k package="2512 [SMD]"]
  Componente5 = Arduino Mega 2560 (Rev3)
  R2 = Resistor [tolerance=±5% resistance=2.2k package="0805 [SMD]"]
  Componente6 = LCD1602-I2C
  J1 = Piezo Speaker

nets:
  N1: kEYPAD_MATRICIAL_1.col1, Componente5.D45
  N2: kEYPAD_MATRICIAL_1.arrow1, Componente5.D43
  N3: kEYPAD_MATRICIAL_1.col2, Componente5.D41
  N4: kEYPAD_MATRICIAL_1.arrow2, Componente5.D39
  N5: kEYPAD_MATRICIAL_1.col3, Componente5.D37
  N6: kEYPAD_MATRICIAL_1.arrow3, Componente5.D35
  N7: kEYPAD_MATRICIAL_1.arrow4, Componente5.D33
  N8: Componente2.TXD, Componente5.A8
  N9: Componente2.RXD, R1.Pin_1, R2.Pin_1
  VCC: Componente2.VCC, Componente5.5V, Componente6.VCC
  GND: Componente2.GND, Componente3.GND, Componente5.GND, R2.Pin_0, Componente6.GND, J1.pin1
  N10: Componente3.SDA, Componente5.D53
  N11: Componente3.SCK, Componente5.D52
  N12: Componente3.MOSI, Componente5.D51
  N13: Componente3.MISO, Componente5.D50
  N14: Componente3.RST, Componente5.D5_PWM
  3.3V: Componente3.3.3V, Componente5.3V3
  N15: R1.Pin_0, Componente5.D14/TX3
  N16: Componente5.D21/SCL, Componente6.SCL
  N17: Componente5.D20/SDA, Componente6.SDA
  N18: Componente5.D23, J1.pin2

notes:
  LCD 1602 I2C
  Keypad 3x4
  HC-05
  RC522
  Buzzer
  Arduino MEGA 2560

custom parts:
  KEYPAD 4x3: KEYPAD matricial de 12 botones, 4 filas x 3 columnas
  RFID-RC522-v2: A simple China made RFID-RC522 Reader; do check the pin labels, as this is a MFRC522 based clone.
  LCD1602-I2C: A standard character display, usually with 2x16 characters. Comes in many colors with LCM1602 IIC attached.
